# Fritzing sketch MicrosoftFlow-LogicApps-Button-Frittzing Project (saved by Fritzing 0.9.3b)
breadboards: 1

parts:
  S1 = Pushbutton [package="[SMD]"]
  R1 = Resistor [tolerance=±5% resistance=1M package="1206 [SMD]"]
  U1 = NodeMCU V1.0
  R2 = Resistor [tolerance=±5% resistance=330 package="1206 [SMD]"]

nets:
  N1: S1.Pin_1, S1.Pin_2, U1.3V3
  N2: S1.Pin_3, S1.Pin_4, R1.Pin_1, R2.Pin_0
  N3: R1.Pin_0, U1.GND
  N4: U1.D0, R2.Pin_1

notes:
  330 ohms
  1M ohms

custom parts:
  NodeMCU V1.0: ESP8266 based NodeMCU
